// Logisim project CircuitsBOOM.circ as structural Verilog: 5 circuits, main circuit Half_Adder
module eight_bit_adder (
  input  B7,
  input  A7,
  input  B6,
  input  A6,
  input  B5,
  input  A5,
  input  B4,
  input  A4,
  input  B3,
  input  A3,
  input  B2,
  input  A2,
  input  B1,
  input  A1,
  input  B0,
  input  A0,
  output S5,
  output Overflow,
  output S7,
  output S6,
  output S4,
  output S3,
  output S2,
  output S1,
  output S0
);

  wire full_adder_2_carry, full_adder_3_carry, full_adder_4_carry, full_adder_5_carry, full_adder_6_carry,
       full_adder_7_carry, half_adder_1_carry;

  Full_Adder full_adder_1 (.Carry_In(full_adder_2_carry), .B(A7), .A(B7), .Sum(S7), .Carry(Overflow));
  Full_Adder full_adder_2 (.Carry_In(full_adder_3_carry), .B(A6), .A(B6), .Sum(S6), .Carry(full_adder_2_carry));
  Full_Adder full_adder_3 (.Carry_In(full_adder_4_carry), .B(A5), .A(B5), .Sum(S5), .Carry(full_adder_3_carry));
  Full_Adder full_adder_4 (.Carry_In(full_adder_5_carry), .B(A4), .A(B4), .Sum(S4), .Carry(full_adder_4_carry));
  Full_Adder full_adder_5 (.Carry_In(full_adder_6_carry), .B(A3), .A(B3), .Sum(S3), .Carry(full_adder_5_carry));
  Full_Adder full_adder_6 (.Carry_In(full_adder_7_carry), .B(A2), .A(B2), .Sum(S2), .Carry(full_adder_6_carry));
  Full_Adder full_adder_7 (.Carry_In(half_adder_1_carry), .B(A1), .A(B1), .Sum(S1), .Carry(full_adder_7_carry));
  Half_Adder half_adder_1 (.A(A0), .B(B0), .Sum(S0), .Carry(half_adder_1_carry));
endmodule

module circuits (
  input  in_1,
  input  in_2,
  output out_3,
  output out_4
);

  xor xor_1 (out_3, in_1, in_2);
  and and_1 (out_4, in_1, in_2);
endmodule

module Half_Adder (
  input  A,
  input  B,
  output Sum,
  output Carry
);

  xor xor_1 (Sum, A, B);
  and and_1 (Carry, A, B);
endmodule

module Full_Adder (
  input  Carry_In,
  input  B,
  input  A,
  output Sum,
  output Carry
);

  wire and_1_out, and_2_out, xor_1_out;

  xor xor_1 (xor_1_out, B, A);
  and and_1 (and_1_out, B, A);
  xor xor_2 (Sum, Carry_In, xor_1_out);
  and and_2 (and_2_out, Carry_In, xor_1_out);
  or or_1 (Carry, and_2_out, and_1_out);
endmodule

module Main (
);

  eight_bit_adder eight_bit_adder_1 ();  // open: B7, A7, B6, A6, B5, A5, B4, A4, B3, A3, B2, A2, B1, A1, B0, A0, S5, Overflow, S7, S6, S4, S3, S2, S1, S0
endmodule
